# Fritzing sketch mbr (saved by Fritzing 0.9.3b)

parts:
  Part1 = Arduino Nano (Rev3.0)
  Part2 = InvenSense MPU6050
  BAT1 = BC9VPC [package=bc9vpc]
  M1 = DC Motor
  M2 = DC Motor
  L298N1 = L298N DC motor driver

nets:
  N1: Part1.D2, Part2.INT
  N2: Part1.D7, L298N1.IN1
  N3: Part1.D8, L298N1.IN2
  N4: Part1.D9, L298N1.ENA
  N5: Part1.D10, L298N1.ENB
  N6: Part1.D11/MOSI, L298N1.IN4
  N7: Part1.D12/MISO, L298N1.IN3
  VIN: Part1.VIN, L298N1.5V
  GND: Part1.GND, Part2.GND, BAT1.V+, L298N1.GND
  5V: Part1.5V, Part2.VCC
  N8: Part1.A5, Part2.SCL
  N9: Part1.A4, Part2.SDA
  N10: BAT1.V-, L298N1.12V
  N11: M1.pin_1, L298N1.OUT4
  N12: M1.pin_2, L298N1.OUT3
  N13: M2.pin_1, L298N1.OUT2
  N14: M2.pin_2, L298N1.OUT1

custom parts:
  L298N DC motor driver: 2x DC motor driver with 78M05 positive voltage regulator (7..35 V) L298N: max 46 V, 2 A Set 5 V Enable jumper to enable 5 V regultor (needed for the L298N) and +5 V output at screw terminal or supply external +5 V at screw terminal Set ENA and/or ENB to +5 V to enable motor permanently or supply ENA and/or ENB with PWM signal IN1 and IN2 set rotation directory for motor A (OUT1/OUT2) IN2 and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
